# Fritzing sketch ComunicacaoArduinoESP8266 (saved by Fritzing 0.9.9b)
circuit board: 8.58211cm x 6.32059cm
breadboards: 1

parts:
  Part2 = RoboCore ESP8266 Adapter
  R2 = Resistor [tolerance=±5% resistance=10k package="1206 [SMD]"]
  S1 = Pushbutton [package="[THT]"]
  U1 = ESP8266 WiFi Module [part_number=ESP8266]
  Part1 = Arduino Uno (Rev3) [part_number=teste]
  LED1 = smd LED [color="Red (633nm)" package="0603 [SMD]"]

nets:
  N1: Part2.TXL, U1.TXD
  GND: Part2.GND, R2.Pin_0, S1.Pin_1, S1.Pin_2, U1.GND, Part1.GND
  N2: Part2.CH_PD, Part2.CP, U1.CH_PD
  N3: Part2.GPIO2, Part2.IO2, U1.GPIO_2, LED1.anode
  N4: Part2.RST, S1.Pin_3, S1.Pin_4, U1.RST
  N5: Part2.GPIO0, Part2.IO0, U1.GPIO_0
  VCC: Part2.VCC, Part2.3V3, U1.VCC
  N6: Part2.RXL, U1.RXD
  N7: Part2.TXH, Part1.D1/TX
  N8: Part2.RXH, Part1.D0/RX
  VIN: Part2.VIN, Part1.5V
  N9: R2.Pin_1, LED1.cathode

custom parts:
  ESP8266 WiFi Module: Generic WiFi Module based on the ESP8266 with onboard PCB antenna and UART communications

// code stored in the sketch: BareMinimum.ino
void setup(){

}

void loop(){

}

// code stored in the sketch: sketch_sep14a.ino
void setup() {
  // put your setup code here, to run once:
  Serial.begin(9600);
  pinMode(13, OUTPUT);
}

int pisca(){
  digitalWrite(13, HIGH);
  delay(500);
  digitalWrite(13, LOW);
  delay(500);
}

int maior(int *v, int n){
  pisca();
  if(n==1){
    return v[0];
  }
  
  int maiorRec = maior(v, n-1);
  if (maiorRec > v[n-1])
    return maiorRec;
  else
    return v[n-1];
  
}

void loop() {
  // put your main code here, to run repeatedly:
  int v[] = {5,3,6,1,7,8,-5};
  int m = maior(v,7);
  delay(3000);

}
