# Fritzing sketch ESP8266comoServidorWeb (saved by Fritzing 0.9.9b)
circuit board: 8.58211cm x 6.32059cm
breadboards: 1

parts:
  Part2 = RoboCore ESP8266 Adapter
  R2 = Resistor [tolerance=±5% resistance=10k package="1206 [SMD]"]
  S1 = Pushbutton [package="[THT]"]
  U1 = ESP8266 WiFi Module [part_number=ESP8266]
  Part1 = Arduino Uno (Rev3) [part_number=teste]
  LED1 = smd LED [color="Red (633nm)" package="0603 [SMD]"]

nets:
  N1: Part2.TXL, U1.TXD
  GND: Part2.GND, R2.Pin_0, S1.Pin_1, S1.Pin_2, U1.GND, Part1.GND
  N2: Part2.CH_PD, Part2.CP, U1.CH_PD
  N3: Part2.GPIO2, Part2.IO2, U1.GPIO_2, LED1.anode
  N4: Part2.RST, S1.Pin_3, S1.Pin_4, U1.RST
  N5: Part2.GPIO0, Part2.IO0, U1.GPIO_0
  VCC: Part2.VCC, Part2.3V3, U1.VCC
  N6: Part2.RXL, U1.RXD
  N7: Part2.TXH, Part1.D1/TX
  N8: Part2.RXH, Part1.D0/RX
  VIN: Part2.VIN, Part1.5V
  N9: R2.Pin_1, LED1.cathode

custom parts:
  ESP8266 WiFi Module: Generic WiFi Module based on the ESP8266 with onboard PCB antenna and UART communications

// code stored in the sketch: ArduinoCode.ino
/*******************************************************************************
* RoboCore - ESP8266 Primeiros Passos com Arduino
* Codigo utilizado para enviar comandos AT atraves do monitor serial da Arduino
* IDE.
*******************************************************************************/  

#include "SoftwareSerial.h"

SoftwareSerial ESP_Serial(10, 11); // RX, TX
int valorSensor;
int valorSensorAntigo = 0;
char buffer[1024];
unsigned long ultimoEnvio = 0;
void setup(){
  pinMode(10, INPUT);
  pinMode(11, OUTPUT);
  Serial.begin(9600);
  ESP_Serial.begin(115200);
}

void envia(char * dados){
  Serial.print("Enviando ");
  Serial.print(dados);
  ESP_Serial.write(dados);
  
}

void loop(){
  if (ESP_Serial.available()){
    Serial.write(ESP_Serial.read());
  }
  
  if (Serial.available()){
    ESP_Serial.write(Serial.read());
  }

  valorSensor = analogRead(A0);
  valorSensor = map(valorSensor, 0,1023, 0, 10);

  if ( abs(valorSensorAntigo - valorSensor) >= 1 && abs(millis() - ultimoEnvio) > 2000){
     ultimoEnvio = millis();
     valorSensorAntigo = valorSensor;
     sprintf(buffer,"%d",valorSensor);
     envia(buffer);
  }
  
  
  
}

// code stored in the sketch: BareMinimum.ino
void setup(){

}

void loop(){

}

// code stored in the sketch: Esp8266Code.ino
/*
  Basic ESP8266 MQTT example
  This sketch demonstrates the capabilities of the pubsub library in combination
  with the ESP8266 board/library.
  It connects to an MQTT server then:
  - publishes "hello world" to the topic "outTopic" every two seconds
  - subscribes to the topic "inTopic", printing out any messages
    it receives. NB - it assumes the received payloads are strings not binary
  - If the first character of the topic "inTopic" is an 1, switch ON the ESP Led,
    else switch it off
  It will reconnect to the server if the connection is lost using a blocking
  reconnect function. See the 'mqtt_reconnect_nonblocking' example for how to
  achieve the same result without blocking the main loop.
  To install the ESP8266 board, (using Arduino 1.6.4+):
  - Add the following 3rd party board manager under "File -> Preferences -> Additional Boards Manager URLs":
       http://arduino.esp8266.com/stable/package_esp8266com_index.json
  - Open the "Tools -> Board -> Board Manager" and click install for the ESP8266"
  - Select your ESP8266 in "Tools -> Board"
*/

#include <ESP8266WiFi.h>
#include <PubSubClient.h>

// Update these with values suitable for your network.

const char* ssid = "HouseTG";
const char* password = "House769";
const char* mqtt_server = "mqtt.lt.gwachs.com";

WiFiClient espClient;
PubSubClient client(espClient);
unsigned long lastMsg = 0;
#define MSG_BUFFER_SIZE	(50)
char msg[MSG_BUFFER_SIZE];
int value = 0;

void setup_wifi() {

  delay(10);
  // We start by connecting to a WiFi network
  Serial.println();
  Serial.print("Connecting to ");
  Serial.println(ssid);

  WiFi.mode(WIFI_STA);
  WiFi.begin(ssid, password);

  while (WiFi.status() != WL_CONNECTED) {
    delay(500);
    Serial.print(".");
  }

  randomSeed(micros());

  Serial.println("");
  Serial.println("WiFi connected");
  Serial.println("IP address: ");
  Serial.println(WiFi.localIP());
}

void callback(char* topic, byte* payload, unsigned int length) {
  Serial.print("Message arrived [");
  Serial.print(topic);
  Serial.print("] ");
  for (int i = 0; i < length; i++) {
    Serial.print((char)payload[i]);
  }
  Serial.println();

  // Switch on the LED if an 1 was received as first character
  if ((char)payload[0] == '1') {
    digitalWrite(BUILTIN_LED, LOW);   // Turn the LED on (Note that LOW is the voltage level
    // but actually the LED is on; this is because
    // it is active low on the ESP-01)
  } else {
    digitalWrite(BUILTIN_LED, HIGH);  // Turn the LED off by making the voltage HIGH
  }

}

void reconnect() {
  // Loop until we're reconnected
  while (!client.connected()) {
    Serial.print("Attempting MQTT connection...");
    // Create a random client ID
    String clientId = "ESP8266Client-";
    clientId += String(random(0xffff), HEX);
    // Attempt to connect
    if (client.connect(clientId.c_str())) {
      Serial.println("connected");
      // Once connected, publish an announcement...
      client.publish("outTopic", "hello world");
      // ... and resubscribe
      client.subscribe("inTopic");
    } else {
      Serial.print("failed, rc=");
      Serial.print(client.state());
      Serial.println(" try again in 5 seconds");
      // Wait 5 seconds before retrying
      delay(5000);
    }
  }
}

void setup() {
  pinMode(BUILTIN_LED, OUTPUT);     // Initialize the BUILTIN_LED pin as an output
  Serial.begin(115200);
  setup_wifi();
  client.setServer(mqtt_server, 1883);
  client.setCallback(callback);
}

void enviaDadosDaSerial() {
  client.publish("Serial", Serial.readString().c_str());
}

void loop() {
  if (Serial.available()) {
    enviaDadosDaSerial();
  }

  if (!client.connected()) {
    reconnect();
  }
  client.loop();
}

// code stored in the sketch: sketch_sep14a.ino
void setup() {
  // put your setup code here, to run once:
  Serial.begin(9600);
  pinMode(13, OUTPUT);
}

int pisca(){
  digitalWrite(13, HIGH);
  delay(500);
  digitalWrite(13, LOW);
  delay(500);
}

int maior(int *v, int n){
  pisca();
  if(n==1){
    return v[0];
  }
  
  int maiorRec = maior(v, n-1);
  if (maiorRec > v[n-1])
    return maiorRec;
  else
    return v[n-1];
  
}

void loop() {
  // put your main code here, to run repeatedly:
  int v[] = {5,3,6,1,7,8,-5};
  int m = maior(v,7);
  delay(3000);

}
