# Fritzing sketch programadorUnoEsp8266 (saved by Fritzing 0.9.9b)
breadboards: 1

parts:
  Part1 = Arduino Uno (Rev3) [part_number=teste]
  Part2 = RoboCore ESP8266 Adapter
  U1 = ESP8266 WiFi Module [part_number=ESP8266]
  S1 = Pushbutton [package="[THT]"]

nets:
  N1: Part1.D0/RX, Part2.RXH
  N2: Part1.D1/TX, Part2.TXH
  5V: Part1.5V, Part2.VIN
  GND: Part1.GND, Part2.GND, Part2.GPIO0, Part2.IO0, U1.GPIO_0, U1.GND, S1.Pin_1, S1.Pin_2
  N3: Part2.TXL, U1.TXD
  N4: Part2.CH_PD, Part2.CP, U1.CH_PD
  N5: Part2.GPIO2, Part2.IO2, U1.GPIO_2
  N6: Part2.RST, U1.RST, S1.Pin_3, S1.Pin_4
  VCC: Part2.VCC, Part2.3V3, U1.VCC
  N7: Part2.RXL, U1.RXD

custom parts:
  ESP8266 WiFi Module: Generic WiFi Module based on the ESP8266 with onboard PCB antenna and UART communications

// code stored in the sketch: BareMinimum.ino
void setup(){

}

void loop(){

}

// code stored in the sketch: sketch_sep14a.ino
void setup() {
  // put your setup code here, to run once:
  Serial.begin(9600);
  pinMode(13, OUTPUT);
}

int pisca(){
  digitalWrite(13, HIGH);
  delay(500);
  digitalWrite(13, LOW);
  delay(500);
}

int maior(int *v, int n){
  pisca();
  if(n==1){
    return v[0];
  }
  
  int maiorRec = maior(v, n-1);
  if (maiorRec > v[n-1])
    return maiorRec;
  else
    return v[n-1];
  
}

void loop() {
  // put your main code here, to run repeatedly:
  int v[] = {5,3,6,1,7,8,-5};
  int m = maior(v,7);
  delay(3000);

}
